# Fritzing sketch Wetterstation (saved by Fritzing 1.0.1rc)
breadboards: 1

parts:
  SOM1 = Daisy Seed [chip_label=IC package="DIP (Dual Inline) [THT]"]
  R1 = Temperature Sensor (Thermistor) [thermistor_type=NTC package=THT]
  R2 = Resistor [tolerance=±5% power=0.25W resistance=220 package=THT]

nets:
  N1: SOM1.pin_20, SOM1.pin_40, R1.pin_1, R2.Pin_0, R2.Pin_1
  N2: SOM1.pin_21, SOM1.pin_28, R1.pin_0

custom parts:
  Daisy Seed: Daisy is an embedded platform for music. It features everything you need for creating high fidelity audio hardware devices. Just plug in a USB cable and start making sound! No soldering required.
